// Logisim project not_gate.circ as structural Verilog
module main (
  input  a,
  output y
);

  not_gate not_gate_1 (.a(a), .y(y));
endmodule

// VHDL entity not_gate, as the project stores it:
LIBRARY ieee;
USE ieee.std_logic_1164.all;

ENTITY not_gate IS
    PORT (
        a : IN std_logic;
        y : OUT std_logic
    );
END not_gate;

ARCHITECTURE behavior OF not_gate IS
BEGIN
    y <= NOT a;
END behavior;
